# Fritzing sketch HeadBlaster_circuit_schematic (saved by Fritzing 0.8.7b)
breadboards: 1
stripboards: 2

parts:
  U1 = RELAY-2 [package=relay-g5v]
  元件1 = Arduino Uno (Rev3)
  VCC1 = Battery
  VCC2 = Battery
  S2 = H-Bridge with L298N
  S3 = Square Pushbutton

nets:
  N1: U1.2, 元件1.D12/MISO
  N2: U1.5, S3.leg1
  GND: U1.9, 元件1.GND, VCC1.-, VCC2.-, S2.GND, S2.M1-01, S2.M2-02, S3.leg0
  N3: U1.10, VCC1.+
  N4: 元件1.D9_PWM, S2.IN2
  N5: 元件1.D10_PWM/SS, S2.IN1
  N6: 元件1.D5_PWM, S2.IN4
  N7: 元件1.D6_PWM, S2.IN3
  N8: VCC2.+, S2.12V

notes:
  ITV2050
  POWER 24V
  POWER 12V
  Pressure Regulator
  SYJ712(valve)

custom parts:
  H-Bridge with L298N: h-bridge
